# Fritzing sketch CIRCUIT 3.0 (saved by Fritzing 0.9.3b)
circuit board: 8.46667cm x 5.64444cm
perfboards: 1

parts:
  Micro_bit1 = Microbit
  Εξάρτημα1 = Logic Level Converter
  hc-sr1 = hc-sr04
  BAT3 = Battery Holders [package=battcon_12mm]
  Εξάρτημα4 = NCP1400 Step-Up Breakout
  U2 = 3.5mm Audio Jack [package=audio-jack]

nets:
  GND: Micro_bit1.GND, Εξάρτημα1.GND, hc-sr1.GND, BAT3.-, Εξάρτημα4.GND, U2.SLEEVE
  N1: Micro_bit1.3V, Εξάρτημα1.LV, BAT3.+, Εξάρτημα4.VIN
  N2: Micro_bit1.0, U2.RIGHT, U2.LEFT
  N3: Micro_bit1.1, Εξάρτημα1.RX_LV
  N4: Micro_bit1.2, Εξάρτημα1.RX2_LV
  N5: Εξάρτημα1.RX_HV, hc-sr1.Trig
  N6: Εξάρτημα1.HV, hc-sr1.VCC, Εξάρτημα4.VOUT
  N7: Εξάρτημα1.RX2_HV, hc-sr1.Echo

custom parts:
  Microbit: BBC Microbit Fritzing part
